# Fritzing sketch bluetooth-arduino-buzzer (saved by Fritzing 0.9.3b)

parts:
  Componente1 = Arduino Uno (Rev3)
  Componente2 = Bluetooth HC-05 Macho
  J1 = Piezo Speaker

nets:
  GND: Componente1.GND, Componente2.GND, J1.pin1
  N1: Componente1.D2, Componente2.TXD
  N2: Componente1.D3_PWM, Componente2.RXD
  N3: Componente1.D4, J1.pin2
  5V: Componente1.5V, Componente2.VCC
